// Logisim project discrete-project.circ as structural Verilog: 2 circuits, main circuit main
module main (
);

  // AND_Gate and_1 is placed but not wired
  // OR_Gate or_1 is placed but not wired
  // OR_Gate or_2 is placed but not wired
endmodule

module Muller_C (
  input  X,
  input  Y,
  output Z
);

  wire and_1_out, and_2_out, or_1_out;

  or or_1 (or_1_out, Z, X);
  and and_1 (and_1_out, or_1_out, Y);
  and and_2 (and_2_out, X, Z);
  or or_2 (Z, and_1_out, and_2_out);
endmodule
